// Logisim project prac_7.circ as structural Verilog: 1 circuit, main circuit main
module main (
  input  BB_3,
  input  BB_2,
  input  BB_1,
  input  BB_0,
  input  BA_3,
  input  BA_2,
  input  BA_1,
  input  BA_0,
  input  add_sub,
  output out_10
);

  wire and_1_out, and_2_out, and_3_out, and_4_out, and_5_out, and_6_out, and_7_out, and_8_out, and_9_out,
       and_14_out, and_19_out, and_24_out, nand_1_out, nand_2_out, nand_3_out, nand_4_out, nand_5_out,
       nand_6_out, nand_7_out, nand_8_out, nand_9_out, nand_10_out, nand_11_out, nand_12_out, nand_13_out,
       nand_14_out, nand_15_out, nand_16_out, nand_17_out, nand_18_out, nand_19_out, nand_20_out,
       nand_21_out, nand_22_out, nand_23_out, nand_24_out, nand_25_out, nand_26_out, nand_27_out,
       nand_28_out, nand_29_out, nand_30_out, nand_31_out, nand_32_out, nand_33_out, nand_34_out,
       nand_35_out, nand_36_out, nand_37_out, nand_38_out, nand_39_out, nand_40_out, nand_41_out,
       nand_42_out, nand_43_out, nand_44_out, nand_45_out, nand_46_out, nand_47_out, nand_48_out,
       nand_49_out, nand_50_out, nand_51_out, nand_52_out, nand_53_out, nand_54_out, nand_55_out,
       nand_56_out, nand_57_out, nand_58_out, nand_59_out, nand_60_out, nand_61_out, nand_62_out,
       nand_63_out, nand_64_out, not_1_out, not_2_out, not_3_out, not_4_out, not_5_out, not_6_out, not_7_out,
       not_8_out, not_9_out, not_10_out, not_11_out, not_12_out, not_13_out, not_14_out, not_15_out,
       not_16_out, not_17_out, not_18_out, or_1_out, or_2_out, or_3_out, undriven, undriven_2, undriven_3,
       undriven_4, undriven_5, undriven_6, undriven_7, undriven_8, undriven_9, xor_1_out, xor_2_out,
       xor_3_out, xor_4_out, xor_5_out, xor_6_out, xor_7_out, xor_8_out, xor_9_out, xor_10_out, xor_11_out,
       xor_12_out;

  xor xor_1 (xor_1_out, BA_3, add_sub);
  xor xor_2 (xor_2_out, BA_2, add_sub);
  xor xor_3 (xor_3_out, BA_1, add_sub);
  xor xor_4 (xor_4_out, BA_0, add_sub);
  xor xor_5 (xor_5_out, xor_4_out, BB_0);
  and and_1 (and_1_out, xor_4_out, BB_0);
  xor xor_6 (xor_6_out, xor_3_out, BB_1);
  and and_2 (and_2_out, xor_3_out, BB_1);
  xor xor_7 (xor_7_out, xor_2_out, BB_2);
  and and_3 (and_3_out, xor_2_out, BB_2);
  xor xor_8 (xor_8_out, xor_1_out, BB_3);
  and and_4 (and_4_out, xor_1_out, BB_3);
  xor xor_9 (xor_9_out, xor_5_out, add_sub);
  and and_5 (and_5_out, xor_5_out, add_sub);
  xor xor_10 (xor_10_out, xor_6_out, or_1_out);
  and and_6 (and_6_out, xor_6_out, or_1_out);
  xor xor_11 (xor_11_out, xor_7_out, or_2_out);
  and and_7 (and_7_out, xor_7_out, or_2_out);
  xor xor_12 (xor_12_out, xor_8_out, or_3_out);
  and and_8 (and_8_out, xor_8_out, or_3_out);
  or or_1 (or_1_out, and_5_out, and_1_out);
  or or_2 (or_2_out, and_6_out, and_2_out);
  or or_3 (or_3_out, and_7_out, and_3_out);
  or or_4 (out_10, and_8_out, and_4_out);
  not not_1 (not_1_out, undriven_6);
  not not_2 (not_2_out, undriven_5);
  not not_3 (not_3_out, undriven);
  not not_4 (not_4_out, undriven_2);
  not not_5 (not_5_out, undriven_3);
  not not_6 (not_6_out, undriven_4);
  and and_9 (and_9_out, not_1_out, not_1_out);
  nand nand_1 (nand_1_out, undriven, and_9_out);
  nand nand_2 (nand_2_out, not_3_out, and_9_out);
  nand nand_3 (nand_3_out, undriven_2, and_9_out);
  nand nand_4 (nand_4_out, not_4_out, and_9_out);
  nand nand_5 (nand_5_out, undriven_3, and_9_out);
  nand nand_6 (nand_6_out, not_5_out, and_9_out);
  nand nand_7 (nand_7_out, undriven_4, and_9_out);
  nand nand_8 (nand_8_out, not_6_out, and_9_out);
  nand nand_9 (nand_9_out, nand_1_out, nand_10_out);
  nand nand_10 (nand_10_out, nand_9_out, nand_2_out);
  nand nand_11 (nand_11_out, nand_3_out, nand_12_out);
  nand nand_12 (nand_12_out, nand_11_out, nand_4_out);
  nand nand_13 (nand_13_out, nand_5_out, nand_14_out);
  nand nand_14 (nand_14_out, nand_13_out, nand_6_out);
  nand nand_15 (nand_15_out, nand_7_out, nand_16_out);
  nand nand_16 (nand_16_out, nand_15_out, nand_8_out);
  // AND_Gate and_10 has open pins: in0=nand_9_out, in1=and_9_out, out=open
  // AND_Gate and_11 has open pins: in0=nand_11_out, in1=and_9_out, out=open
  // AND_Gate and_12 has open pins: in0=nand_13_out, in1=and_9_out, out=open
  // AND_Gate and_13 has open pins: in0=nand_15_out, in1=and_9_out, out=open
  not not_7 (not_7_out, undriven);
  not not_8 (not_8_out, undriven_2);
  not not_9 (not_9_out, undriven_3);
  not not_10 (not_10_out, undriven_4);
  and and_14 (and_14_out, undriven_6, not_2_out);
  nand nand_17 (nand_17_out, undriven, and_14_out);
  nand nand_18 (nand_18_out, not_7_out, and_14_out);
  nand nand_19 (nand_19_out, undriven_2, and_14_out);
  nand nand_20 (nand_20_out, not_8_out, and_14_out);
  nand nand_21 (nand_21_out, undriven_3, and_14_out);
  nand nand_22 (nand_22_out, not_9_out, and_14_out);
  nand nand_23 (nand_23_out, undriven_4, and_14_out);
  nand nand_24 (nand_24_out, not_10_out, and_14_out);
  nand nand_25 (nand_25_out, nand_17_out, nand_26_out);
  nand nand_26 (nand_26_out, nand_25_out, nand_18_out);
  nand nand_27 (nand_27_out, nand_19_out, nand_28_out);
  nand nand_28 (nand_28_out, nand_27_out, nand_20_out);
  nand nand_29 (nand_29_out, nand_21_out, nand_30_out);
  nand nand_30 (nand_30_out, nand_29_out, nand_22_out);
  nand nand_31 (nand_31_out, nand_23_out, nand_32_out);
  nand nand_32 (nand_32_out, nand_31_out, nand_24_out);
  // AND_Gate and_15 has open pins: in0=nand_25_out, in1=and_14_out, out=open
  // AND_Gate and_16 has open pins: in0=nand_27_out, in1=and_14_out, out=open
  // AND_Gate and_17 has open pins: in0=nand_29_out, in1=and_14_out, out=open
  // AND_Gate and_18 has open pins: in0=nand_31_out, in1=and_14_out, out=open
  not not_11 (not_11_out, undriven);
  not not_12 (not_12_out, undriven_2);
  not not_13 (not_13_out, undriven_3);
  not not_14 (not_14_out, undriven_4);
  nand nand_33 (nand_33_out, undriven, and_19_out);
  nand nand_34 (nand_34_out, not_11_out, and_19_out);
  nand nand_35 (nand_35_out, undriven_2, and_19_out);
  nand nand_36 (nand_36_out, not_12_out, and_19_out);
  nand nand_37 (nand_37_out, undriven_3, and_19_out);
  nand nand_38 (nand_38_out, not_13_out, and_19_out);
  nand nand_39 (nand_39_out, undriven_4, and_19_out);
  nand nand_40 (nand_40_out, not_14_out, and_19_out);
  and and_19 (and_19_out, undriven_7, undriven_7);
  nand nand_41 (nand_41_out, nand_33_out, nand_42_out);
  nand nand_42 (nand_42_out, nand_41_out, nand_34_out);
  nand nand_43 (nand_43_out, nand_35_out, nand_44_out);
  nand nand_44 (nand_44_out, nand_43_out, nand_36_out);
  nand nand_45 (nand_45_out, nand_37_out, nand_46_out);
  nand nand_46 (nand_46_out, nand_45_out, nand_38_out);
  nand nand_47 (nand_47_out, nand_39_out, nand_48_out);
  nand nand_48 (nand_48_out, nand_47_out, nand_40_out);
  not not_15 (not_15_out, undriven);
  not not_16 (not_16_out, undriven_2);
  not not_17 (not_17_out, undriven_3);
  not not_18 (not_18_out, undriven_4);
  // AND_Gate and_20 has open pins: in0=nand_41_out, in1=and_19_out, out=open
  // AND_Gate and_21 has open pins: in0=nand_43_out, in1=and_19_out, out=open
  // AND_Gate and_22 has open pins: in0=nand_45_out, in1=and_19_out, out=open
  // AND_Gate and_23 has open pins: in0=nand_47_out, in1=and_19_out, out=open
  nand nand_49 (nand_49_out, undriven, and_24_out);
  nand nand_50 (nand_50_out, not_15_out, and_24_out);
  nand nand_51 (nand_51_out, undriven_2, and_24_out);
  nand nand_52 (nand_52_out, not_16_out, and_24_out);
  nand nand_53 (nand_53_out, undriven_3, and_24_out);
  nand nand_54 (nand_54_out, not_17_out, and_24_out);
  nand nand_55 (nand_55_out, undriven_4, and_24_out);
  nand nand_56 (nand_56_out, not_18_out, and_24_out);
  and and_24 (and_24_out, undriven_8, undriven_9);
  nand nand_57 (nand_57_out, nand_49_out, nand_58_out);
  nand nand_58 (nand_58_out, nand_57_out, nand_50_out);
  nand nand_59 (nand_59_out, nand_51_out, nand_60_out);
  nand nand_60 (nand_60_out, nand_59_out, nand_52_out);
  nand nand_61 (nand_61_out, nand_53_out, nand_62_out);
  nand nand_62 (nand_62_out, nand_61_out, nand_54_out);
  nand nand_63 (nand_63_out, nand_55_out, nand_64_out);
  nand nand_64 (nand_64_out, nand_63_out, nand_56_out);
  // AND_Gate and_25 has open pins: in0=nand_57_out, in1=and_24_out, out=open
  // AND_Gate and_26 has open pins: in0=nand_59_out, in1=and_24_out, out=open
  // AND_Gate and_27 has open pins: in0=nand_61_out, in1=and_24_out, out=open
  // AND_Gate and_28 has open pins: in0=nand_63_out, in1=and_24_out, out=open
endmodule
