// Logisim project practice.circ as structural Verilog: 2 circuits, main circuit main
module main (
);

  arithmetic_circuit arithmetic_circuit_1 ();  // open: B1_0, B2_5, B1_6, B2_6, B1_7, B2_7, B1_1, B2_1, B1_2, B2_2, B2_0, B1_3, B2_3, B1_4, B2_4, B1_5, S_5, S_6, S_7, S_8, S_1, S_0, S_2, S_3, S_4
endmodule

module arithmetic_circuit (
  input  B1_0,
  input  B2_0,
  input  B1_1,
  input  B2_1,
  input  B1_2,
  input  B2_2,
  input  B1_3,
  input  B2_3,
  input  B1_4,
  input  B2_4,
  input  B1_5,
  input  B2_5,
  input  B1_6,
  input  B2_6,
  input  B1_7,
  input  B2_7,
  output S_0,
  output S_1,
  output S_2,
  output S_3,
  output S_4,
  output S_5,
  output S_6,
  output S_7,
  output S_8
);

  wire and_1_out, and_2_out, and_3_out, and_4_out, and_5_out, and_6_out, and_7_out, and_8_out, and_9_out,
       and_10_out, and_11_out, and_12_out, and_13_out, and_14_out, and_15_out, or_1_out, or_2_out, or_3_out,
       or_4_out, or_5_out, or_6_out, xor_2_out, xor_3_out, xor_4_out, xor_5_out, xor_6_out, xor_7_out,
       xor_8_out;

  xor xor_1 (S_0, B1_0, B2_0);
  and and_1 (and_1_out, B1_0, B2_0);
  xor xor_2 (xor_2_out, B1_1, B2_1);
  and and_2 (and_2_out, B1_1, B2_1);
  xor xor_3 (xor_3_out, B1_2, B2_2);
  and and_3 (and_3_out, B1_2, B2_2);
  xor xor_4 (xor_4_out, B1_3, B2_3);
  and and_4 (and_4_out, B1_3, B2_3);
  xor xor_5 (xor_5_out, B1_4, B2_4);
  and and_5 (and_5_out, B1_4, B2_4);
  xor xor_6 (xor_6_out, B1_5, B2_5);
  and and_6 (and_6_out, B1_5, B2_5);
  xor xor_7 (xor_7_out, B1_6, B2_6);
  and and_7 (and_7_out, B1_6, B2_6);
  xor xor_8 (xor_8_out, B1_7, B2_7);
  and and_8 (and_8_out, B1_7, B2_7);
  xor xor_9 (S_1, xor_2_out, and_1_out);
  and and_9 (and_9_out, xor_2_out, and_1_out);
  or or_1 (or_1_out, and_9_out, and_2_out);
  xor xor_10 (S_2, xor_3_out, or_1_out);
  and and_10 (and_10_out, xor_3_out, or_1_out);
  or or_2 (or_2_out, and_10_out, and_3_out);
  xor xor_11 (S_3, xor_4_out, or_2_out);
  and and_11 (and_11_out, xor_4_out, or_2_out);
  or or_3 (or_3_out, and_11_out, and_4_out);
  xor xor_12 (S_4, xor_5_out, or_3_out);
  and and_12 (and_12_out, xor_5_out, or_3_out);
  or or_4 (or_4_out, and_12_out, and_5_out);
  xor xor_13 (S_5, xor_6_out, or_4_out);
  and and_13 (and_13_out, xor_6_out, or_4_out);
  or or_5 (or_5_out, and_13_out, and_6_out);
  xor xor_14 (S_6, xor_7_out, or_5_out);
  and and_14 (and_14_out, xor_7_out, or_5_out);
  or or_6 (or_6_out, and_14_out, and_7_out);
  xor xor_15 (S_7, xor_8_out, or_6_out);
  and and_15 (and_15_out, xor_8_out, or_6_out);
  or or_7 (S_8, and_15_out, and_8_out);
endmodule
