// Logisim project practice_2.circ as structural Verilog
module half_adder (
  input  Bit_0,
  input  Bit_1,
  output Sum,
  output Carry_out
);

  xor xor_1 (Sum, Bit_0, Bit_1);
  and and_1 (Carry_out, Bit_0, Bit_1);
endmodule

module full_adder (
  input  Bit_0,
  input  Bit_1,
  input  Carry_in,
  output Sum,
  output Carry_out
);

  wire and_1_out, and_2_out, xor_1_out;

  xor xor_1 (xor_1_out, Bit_0, Bit_1);
  and and_1 (and_1_out, Bit_0, Bit_1);
  xor xor_2 (Sum, xor_1_out, Carry_in);
  and and_2 (and_2_out, xor_1_out, Carry_in);
  or or_1 (Carry_out, and_2_out, and_1_out);
endmodule

module arithmetic_circuit (
  input  Bit_A_0,
  input  Bit_B_0,
  input  negate_add_one,
  input  Bit_A_1,
  input  Bit_B_1,
  input  Bit_A_2,
  input  Bit_B_2,
  input  Bit_A_3,
  input  Bit_B_3,
  input  Bit_A_4,
  input  Bit_B_4,
  input  Bit_A_5,
  input  Bit_B_5,
  input  Bit_A_6,
  input  Bit_B_6,
  input  Bit_A_7,
  input  Bit_B_7,
  output Sum_0,
  output Sum_1,
  output Sum_2,
  output Sum_3,
  output Sum_4,
  output Sum_5,
  output Sum_6,
  output Sum_7,
  output Sum_8
);

  wire full_adder_1_carry_out, full_adder_2_carry_out, full_adder_3_carry_out, full_adder_4_carry_out,
       full_adder_5_carry_out, full_adder_6_carry_out, full_adder_7_carry_out;

  full_adder full_adder_1 (
    .Bit_0(Bit_A_0), .Bit_1(Bit_B_0), .Carry_in(negate_add_one), .Sum(Sum_0),
    .Carry_out(full_adder_1_carry_out));
  full_adder full_adder_2 (
    .Bit_0(Bit_A_1), .Bit_1(Bit_B_1), .Carry_in(full_adder_1_carry_out), .Sum(Sum_1),
    .Carry_out(full_adder_2_carry_out));
  full_adder full_adder_3 (
    .Bit_0(Bit_A_2), .Bit_1(Bit_B_2), .Carry_in(full_adder_2_carry_out), .Sum(Sum_2),
    .Carry_out(full_adder_3_carry_out));
  full_adder full_adder_4 (
    .Bit_0(Bit_A_3), .Bit_1(Bit_B_3), .Carry_in(full_adder_3_carry_out), .Sum(Sum_3),
    .Carry_out(full_adder_4_carry_out));
  full_adder full_adder_5 (
    .Bit_0(Bit_A_4), .Bit_1(Bit_B_4), .Carry_in(full_adder_4_carry_out), .Sum(Sum_4),
    .Carry_out(full_adder_5_carry_out));
  full_adder full_adder_6 (
    .Bit_0(Bit_A_5), .Bit_1(Bit_B_5), .Carry_in(full_adder_5_carry_out), .Sum(Sum_5),
    .Carry_out(full_adder_6_carry_out));
  full_adder full_adder_7 (
    .Bit_0(Bit_A_6), .Bit_1(Bit_B_6), .Carry_in(full_adder_6_carry_out), .Sum(Sum_6),
    .Carry_out(full_adder_7_carry_out));
  full_adder full_adder_8 (
    .Bit_0(Bit_A_7), .Bit_1(Bit_B_7), .Carry_in(full_adder_7_carry_out), .Sum(Sum_7), .Carry_out(Sum_8));
endmodule

module eight_xor (
  input  input_0,
  input  input_1,
  input  input_2,
  input  input_3,
  input  input_4,
  input  input_5,
  input  input_6,
  input  input_7,
  input  input_8,
  input  input_9,
  input  input_10,
  input  input_11,
  input  input_12,
  input  input_13,
  input  input_14,
  input  input_15,
  output output_0,
  output output_1,
  output output_2,
  output output_3,
  output output_4,
  output output_5,
  output output_6,
  output output_8
);

  xor xor_1 (output_0, input_0, input_1);
  xor xor_2 (output_1, input_2, input_3);
  xor xor_3 (output_2, input_4, input_5);
  xor xor_4 (output_3, input_6, input_7);
  xor xor_5 (output_4, input_8, input_9);
  xor xor_6 (output_5, input_10, input_11);
  xor xor_7 (output_6, input_12, input_13);
  xor xor_8 (output_8, input_14, input_15);
endmodule

module idk (
  input  in_1,
  input  in_2,
  input  in_3,
  input  in_4,
  input  in_5,
  input  in_6,
  input  toggle_output,
  input  in_8,
  input  in_9,
  input  in_10,
  input  in_11,
  input  in_12,
  input  in_13,
  input  in_14,
  input  in_15,
  input  in_16,
  input  in_17,
  input  add_subtract
);

  wire arithmetic_circuit_1_sum_0, arithmetic_circuit_1_sum_1, arithmetic_circuit_1_sum_2,
       arithmetic_circuit_1_sum_3, arithmetic_circuit_1_sum_4, arithmetic_circuit_1_sum_5,
       arithmetic_circuit_1_sum_6, arithmetic_circuit_1_sum_7, arithmetic_circuit_1_sum_8,
       eight_and_1_output_0, eight_and_1_output_1, eight_and_1_output_2, eight_and_1_output_3,
       eight_and_1_output_4, eight_and_1_output_5, eight_and_1_output_6, eight_and_1_output_7,
       eight_xor_1_output_0, eight_xor_1_output_1, eight_xor_1_output_2, eight_xor_1_output_3,
       eight_xor_1_output_4, eight_xor_1_output_5, eight_xor_1_output_6, eight_xor_1_output_8;

  arithmetic_circuit arithmetic_circuit_1 (
    .negate_add_one(add_subtract), .Bit_A_1(in_2), .Bit_B_1(eight_xor_1_output_1), .Bit_A_2(in_3),
    .Bit_B_2(eight_xor_1_output_2), .Bit_A_3(in_4), .Bit_B_3(eight_xor_1_output_3), .Bit_A_4(in_5),
    .Bit_B_4(eight_xor_1_output_4), .Bit_A_5(in_6), .Bit_B_5(eight_xor_1_output_5), .Bit_A_6(in_8),
    .Bit_B_6(eight_xor_1_output_6), .Bit_A_7(in_9), .Bit_B_7(eight_xor_1_output_8), .Bit_A_0(in_1),
    .Bit_B_0(eight_xor_1_output_0), .Sum_1(arithmetic_circuit_1_sum_1), .Sum_2(arithmetic_circuit_1_sum_2),
    .Sum_3(arithmetic_circuit_1_sum_3), .Sum_4(arithmetic_circuit_1_sum_4),
    .Sum_5(arithmetic_circuit_1_sum_5), .Sum_6(arithmetic_circuit_1_sum_6),
    .Sum_7(arithmetic_circuit_1_sum_7), .Sum_8(arithmetic_circuit_1_sum_8), .Sum_0(arithmetic_circuit_1_sum_0));
  eight_xor eight_xor_1 (
    .input_0(in_10), .input_1(add_subtract), .input_2(in_11), .input_3(add_subtract), .input_4(in_12),
    .input_5(add_subtract), .input_6(in_13), .input_7(add_subtract), .input_8(in_14), .input_9(add_subtract),
    .input_10(in_15), .input_11(add_subtract), .input_12(in_16), .input_13(add_subtract), .input_14(in_17),
    .input_15(add_subtract), .output_0(eight_xor_1_output_0), .output_1(eight_xor_1_output_1),
    .output_2(eight_xor_1_output_2), .output_3(eight_xor_1_output_3), .output_4(eight_xor_1_output_4),
    .output_5(eight_xor_1_output_5), .output_6(eight_xor_1_output_6), .output_8(eight_xor_1_output_8));
  LED led_1 (.in(eight_and_1_output_0));
  eight_and eight_and_1 (
    .intput_0(arithmetic_circuit_1_sum_0), .intput_1(toggle_output), .intput_2(arithmetic_circuit_1_sum_1),
    .intput_3(toggle_output), .intput_4(arithmetic_circuit_1_sum_2), .intput_5(toggle_output),
    .intput_6(arithmetic_circuit_1_sum_3), .intput_7(toggle_output), .intput_8(arithmetic_circuit_1_sum_4),
    .intput_9(toggle_output), .intput_10(arithmetic_circuit_1_sum_5), .intput_11(toggle_output),
    .intput_12(arithmetic_circuit_1_sum_6), .intput_13(toggle_output),
    .intput_14(arithmetic_circuit_1_sum_7), .intput_15(toggle_output), .output_0(eight_and_1_output_0),
    .output_1(eight_and_1_output_1), .output_2(eight_and_1_output_2), .output_3(eight_and_1_output_3),
    .output_4(eight_and_1_output_4), .output_5(eight_and_1_output_5), .output_6(eight_and_1_output_6),
    .output_7(eight_and_1_output_7));
  LED led_2 (.in(eight_and_1_output_1));
  LED led_3 (.in(eight_and_1_output_2));
  LED led_4 (.in(eight_and_1_output_3));
  LED led_5 (.in(eight_and_1_output_4));
  LED led_6 (.in(eight_and_1_output_5));
  LED led_7 (.in(eight_and_1_output_6));
  LED led_8 (.in(eight_and_1_output_7));
  LED led_9 (.in(arithmetic_circuit_1_sum_8));
endmodule

module eight_and (
  input  intput_0,
  input  intput_1,
  input  intput_2,
  input  intput_3,
  input  intput_4,
  input  intput_5,
  input  intput_6,
  input  intput_7,
  input  intput_8,
  input  intput_9,
  input  intput_10,
  input  intput_11,
  input  intput_12,
  input  intput_13,
  input  intput_14,
  input  intput_15,
  output output_0,
  output output_1,
  output output_2,
  output output_3,
  output output_4,
  output output_5,
  output output_6,
  output output_7
);

  and and_1 (output_0, intput_0, intput_1);
  and and_2 (output_1, intput_2, intput_3);
  and and_3 (output_2, intput_4, intput_5);
  and and_4 (output_3, intput_6, intput_7);
  and and_5 (output_4, intput_8, intput_9);
  and and_6 (output_5, intput_10, intput_11);
  and and_7 (output_6, intput_12, intput_13);
  and and_8 (output_7, intput_14, intput_15);
endmodule
