// Logisim project practice_3.circ as structural Verilog: 1 circuit, main circuit main
module main (
  input  in_1,
  input  in_2,
  input  in_3,
  input  in_4,
  input  in_5,
  input  Set,
  input  in_7,
  input  in_8,
  input  Reset,
  input  in_10,
  input  in_11,
  input  in_12,
  input  in_13,
  input  in_14,
  input  in_15,
  input  in_16,
  output out_17,
  output out_18,
  output Stored_Output,
  output out_20,
  output out_21,
  output out_22,
  output out_23,
  output out_24,
  output out_25,
  output out_26
);

  wire and_1_out, and_2_out, multiplexer_2_out, multiplexer_3_out, not_1_out, not_2_out, not_3_out, not_4_out;

  Multiplexer multiplexer_1 (.in0(Stored_Output), .in1(Set), .out(Stored_Output), .sel(not_1_out));
  not not_1 (not_1_out, Reset);
  not not_2 (not_2_out, in_2);
  and and_1 (and_1_out, in_1, not_2_out);
  and and_2 (and_2_out, in_2, in_3);
  Multiplexer multiplexer_2 (.in0(multiplexer_2_out), .in1(in_4), .out(multiplexer_2_out), .sel(in_5));
  Multiplexer multiplexer_3 (.in0(multiplexer_3_out), .in1(in_10), .out(multiplexer_3_out), .sel(not_3_out));
  not not_3 (not_3_out, in_12);
  or or_1 (out_17, and_1_out, and_2_out);
  Multiplexer multiplexer_4 (.in0(out_18), .in1(multiplexer_2_out), .out(out_18), .sel(not_4_out));
  not not_4 (not_4_out, in_5);
  Multiplexer multiplexer_5 (.in0(out_22), .in1(multiplexer_3_out), .out(out_22), .sel(in_12));
  D_Flip_Flop d_ff_1 (.D(in_7), .clk(in_8), .Q(out_20), .Qn(out_21));  // open: preset, reset
  T_Flip_Flop t_ff_1 (.T(in_11), .clk(in_13), .Q(out_23), .Qn(out_24));  // open: reset, preset
  J_K_Flip_Flop j_k_ff_1 (.J(in_14), .K(in_15), .clk(in_16), .Q(out_25), .Qn(out_26));  // open: preset, reset
endmodule
