// Logisim project practice_4.circ as structural Verilog: 1 circuit, main circuit main
module main (
  input  in_1,
  input  in_2,
  input  in_3,
  input  in_4,
  input  in_5,
  input  in_6,
  input  in_7,
  input  in_8,
  output out_9,
  output out_10,
  output out_11,
  output out_12,
  output out_13,
  output out_14,
  output out_15
);

  wire and_1_out, and_2_out, nand_1_out, not_1_out;

  not not_1 (not_1_out, in_2);
  and and_1 (and_1_out, out_9, not_1_out);
  and and_2 (and_2_out, in_1, in_2);
  or or_1 (out_9, and_1_out, and_2_out);
  nand nand_1 (nand_1_out, in_3, out_11);
  nand nand_2 (out_11, nand_1_out, in_4);
  nor nor_1 (out_14, in_7, out_15);
  nor nor_2 (out_15, out_14, in_8);
  D_Flip_Flop d_ff_1 (.D(in_5), .clk(in_6), .Q(out_13));  // open: Qn, preset, reset
  nand nand_3 (out_10, nand_1_out, out_12);
  nand nand_4 (out_12, out_10, in_4);
endmodule
