// Logisim project practice_5.circ as structural Verilog: 1 circuit, main circuit main
module main (
  input  in_1,
  input  in_2,
  input  in_3,
  input  in_4,
  input  in_5,
  input  in_6,
  input  in_7,
  input  in_8,
  input  in_9,
  input  in_10,
  input  in_11,
  input  in_12,
  input  in_13,
  input  in_14,
  input  LOW,
  input  SELECTOR_LOW_MED,
  input  MEDIUM,
  input  SELECTOR_HIGH,
  input  HIGH,
  output out_20,
  output out_21,
  output out_22,
  output out_23,
  output out_24,
  output out_25,
  output out_26
);

  wire and_1_out, and_2_out, and_3_out, and_4_out, and_5_out, and_6_out, and_7_out, and_10_out, and_11_out,
       and_12_out, and_13_out, not_1_out, not_2_out, not_3_out, not_6_out, not_7_out, not_8_out, not_9_out,
       or_2_out, or_3_out;

  not not_1 (not_1_out, in_12);
  and and_1 (and_1_out, in_5, in_5);
  not not_2 (not_2_out, in_13);
  not not_3 (not_3_out, and_1_out);
  and and_2 (and_2_out, in_7, not_1_out);
  and and_3 (and_3_out, in_8, in_12);
  and and_4 (and_4_out, in_9, not_2_out);
  and and_5 (and_5_out, in_10, in_13);
  and and_6 (and_6_out, in_4, in_5);
  not not_4 (out_22, and_6_out);
  and and_7 (and_7_out, not_3_out, in_6);
  not not_5 (out_23, and_7_out);
  not not_6 (not_6_out, SELECTOR_LOW_MED);
  and and_8 (out_20, in_1, not_7_out);
  not not_7 (not_7_out, in_2);
  and and_9 (out_21, in_2, in_3);
  or or_1 (out_24, and_2_out, and_3_out, and_4_out, and_5_out);
  and and_10 (and_10_out, LOW, not_6_out);
  and and_11 (and_11_out, SELECTOR_LOW_MED, MEDIUM);
  or or_2 (or_2_out, and_10_out, and_11_out);
  or or_3 (or_3_out, in_11, in_14);
  not not_8 (not_8_out, in_14);
  and and_12 (and_12_out, HIGH, SELECTOR_HIGH);
  not not_9 (not_9_out, SELECTOR_HIGH);
  and and_13 (and_13_out, not_9_out, or_2_out);
  and and_14 (out_25, or_3_out, not_8_out);
  or or_4 (out_26, and_12_out, and_13_out);

  // Notes on the sheet:
  //   MULTIPLEXER 3:1
endmodule
